# Fritzing sketch oven_thermometer (saved by Fritzing 0.9.3b)
breadboards: 4

parts:
  U1 = NodeMCU V1.0
  LCD1 = 2.8" SPI TFT Module [part_number=MSP2807]
  Part2 = Passive Buzzer  # not connected
  U2 = Mono 2.6W Class D Amplifier [package=8-tdfn-ep]
  LCD2 = 2.8" SPI TFT Module [part_number=MSP2807]
  U3 = ESP8266 NodeMCU LoLin module
  U4 = Mono 2.6W Class D Amplifier [package=8-tdfn-ep]

nets:
  N1: U1.D0, U2.CS
  N2: U1.D1, U2.SO
  N3: U1.D2, LCD1.pin3
  N4: U1.D3, LCD1.pin4
  N5: U1.D4, LCD1.pin5
  3V3: U1.3V3, LCD1.pin1, LCD1.pin8, U2.VCC
  GND: U1.GND, LCD1.pin2, U2.GND
  N6: U1.D5, LCD1.pin7
  N7: U1.D7, LCD1.pin6
  N8: U1.D8, U2.SCK
  GND_2: LCD2.pin1, LCD2.pin8, LCD2.pin16, LCD2.pin17, LCD2.pin18, U3.GND, U4.GND
  3V3_2: LCD2.pin2, U3.3V3, U4.VCC
  N9: LCD2.pin3, U3.D0
  N10: LCD2.pin4, U3.D1
  N11: LCD2.pin5, U3.D2
  N12: LCD2.pin6, U3.D7
  N13: LCD2.pin7, U3.D5
  N14: U3.D3, U4.CS
  N15: U3.D4, U4.SO
  N16: U3.D8, U4.SCK

custom parts:
  NodeMCU V1.0: ESP8266 based NodeMCU
  2.8" SPI TFT Module: A generic 2.8 inch LCD TFT 320x240 display with touchscreen and SD card slot. Uses the ILI9341 controller, like the Adafruit displays of this size uses.
  Mono 2.6W Class D Amplifier: Mono 2.6W Class D Amplifier Datasheet: http://datasheets.maxim-ic.com/en/ds/MAX98300.pdf The MAX98300 mono 2.6W Class D amplifier provides Class AB audio performance with Class D efficiency. This device offers five selectable gain settings (0dB, 3dB, 6dB, 9dB, and 12dB) set by a single gain-select input (GAIN). Active emissions-limiting edge-rate and overshoot control circuitry greatly reduces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
  ESP8266 NodeMCU LoLin module: ESP8266 based NodeMCU
